// Logisim project Finalproject.circ as structural Verilog: 3 circuits, main circuit main
module main (
);

  wire and_1_out, and_2_out, and_3_out, and_4_out, and_5_out, and_6_out, and_7_out, and_8_out, and_9_out,
       and_10_out, and_11_out, clock_1_out, j_k_ff_1_q, j_k_ff_2_q, j_k_ff_3_q, j_k_ff_4_q, j_k_ff_5_q,
       j_k_ff_6_q, j_k_ff_7_q, j_k_ff_8_q, j_k_ff_9_q, j_k_ff_10_q, j_k_ff_11_q, j_k_ff_12_q, not_1_out,
       not_2_out, not_3_out, not_4_out, not_5_out, not_6_out, not_7_out, not_8_out, seven_1_a, seven_1_b,
       seven_1_c, seven_1_d, seven_1_e, seven_1_f, seven_1_g, seven_2_a, seven_2_b, seven_2_c, seven_2_d,
       seven_2_e, seven_2_f, seven_2_g, seven_3_a, seven_3_b, seven_3_c, seven_3_d, seven_3_e, seven_3_f,
       seven_3_g;

  Clock clock_1 (.out(clock_1_out));
  and and_1 (and_1_out, j_k_ff_12_q, j_k_ff_6_q);
  and and_2 (and_2_out, j_k_ff_10_q, j_k_ff_4_q);
  J_K_Flip_Flop j_k_ff_1 (
    .J(1'b1), .clk(and_11_out), .K(1'b1), .Q(j_k_ff_1_q), .preset(1'b0), .reset(1'b0));  // open: Qn, en
  and and_3 (and_3_out, j_k_ff_11_q, j_k_ff_5_q);
  J_K_Flip_Flop j_k_ff_2 (
    .J(1'b1), .clk(and_10_out), .K(1'b1), .Q(j_k_ff_2_q), .preset(1'b0), .reset(1'b0));  // open: Qn, en
  J_K_Flip_Flop j_k_ff_3 (
    .J(1'b1), .clk(clock_1_out), .K(1'b1), .Q(j_k_ff_3_q), .preset(1'b0), .reset(1'b0));  // open: Qn, en
  not not_1 (not_1_out, j_k_ff_1_q);
  J_K_Flip_Flop j_k_ff_4 (
    .J(j_k_ff_3_q), .clk(clock_1_out), .K(j_k_ff_3_q), .Q(j_k_ff_4_q), .preset(1'b0), .reset(and_2_out));  // open: Qn, en
  not not_2 (not_2_out, j_k_ff_5_q);
  J_K_Flip_Flop j_k_ff_5 (
    .J(j_k_ff_1_q), .clk(and_11_out), .K(j_k_ff_1_q), .Q(j_k_ff_5_q), .preset(1'b0), .reset(and_3_out));  // open: Qn, en
  J_K_Flip_Flop j_k_ff_6 (
    .J(j_k_ff_2_q), .clk(and_10_out), .K(j_k_ff_2_q), .Q(j_k_ff_6_q), .preset(1'b0), .reset(and_1_out));  // open: Qn, en
  and and_4 (and_4_out, j_k_ff_3_q, j_k_ff_4_q);
  and and_5 (and_5_out, j_k_ff_1_q, j_k_ff_5_q);
  and and_6 (and_6_out, j_k_ff_2_q, j_k_ff_6_q);
  J_K_Flip_Flop j_k_ff_7 (
    .J(and_6_out), .clk(and_10_out), .K(and_6_out), .Q(j_k_ff_7_q), .preset(1'b0), .reset(1'b0));  // open: Qn, en
  J_K_Flip_Flop j_k_ff_8 (
    .J(and_4_out), .clk(clock_1_out), .K(and_4_out), .Q(j_k_ff_8_q), .preset(1'b0), .reset(1'b0));  // open: Qn, en
  not not_3 (not_3_out, j_k_ff_9_q);
  and and_7 (and_7_out, and_5_out, j_k_ff_9_q);
  J_K_Flip_Flop j_k_ff_9 (
    .J(and_5_out), .clk(and_11_out), .K(and_5_out), .Q(j_k_ff_9_q), .preset(1'b0), .reset(1'b0));  // open: Qn, en
  and and_8 (and_8_out, and_6_out, j_k_ff_7_q);
  and and_9 (and_9_out, and_4_out, j_k_ff_8_q);
  J_K_Flip_Flop j_k_ff_10 (
    .J(and_9_out), .clk(clock_1_out), .K(and_9_out), .Q(j_k_ff_10_q), .preset(1'b0), .reset(and_2_out));  // open: Qn, en
  not not_4 (not_4_out, j_k_ff_11_q);
  J_K_Flip_Flop j_k_ff_11 (
    .J(and_7_out), .clk(and_11_out), .K(and_7_out), .Q(j_k_ff_11_q), .preset(1'b0), .reset(and_3_out));  // open: Qn, en
  J_K_Flip_Flop j_k_ff_12 (
    .J(and_8_out), .clk(and_10_out), .K(and_8_out), .Q(j_k_ff_12_q), .preset(1'b0), .reset(and_1_out));  // open: Qn, en
  and and_10 (and_10_out, not_1_out, not_2_out, not_3_out, not_4_out);
  seven seven_1 (
    .W(j_k_ff_11_q), .X(j_k_ff_9_q), .Y(j_k_ff_5_q), .Z(j_k_ff_1_q), .a(seven_1_a), .b(seven_1_b),
    .c(seven_1_c), .d(seven_1_d), .e(seven_1_e), .f(seven_1_f), .g(seven_1_g));
  not not_5 (not_5_out, j_k_ff_3_q);
  not not_6 (not_6_out, j_k_ff_4_q);
  not not_7 (not_7_out, j_k_ff_8_q);
  not not_8 (not_8_out, j_k_ff_10_q);
  _7_Segment_Display u_7_segment_display_1 (
    .g(seven_2_g), .f(seven_2_f), .a(seven_2_a), .b(seven_2_b), .e(seven_2_e), .d(seven_2_d), .c(seven_2_c));  // open: dp
  _7_Segment_Display u_7_segment_display_2 (
    .g(seven_1_g), .f(seven_1_f), .a(seven_1_a), .b(seven_1_b), .e(seven_1_e), .d(seven_1_d), .c(seven_1_c));  // open: dp
  seven seven_2 (
    .W(j_k_ff_12_q), .X(j_k_ff_7_q), .Y(j_k_ff_6_q), .Z(j_k_ff_2_q), .a(seven_2_a), .b(seven_2_b),
    .c(seven_2_c), .d(seven_2_d), .e(seven_2_e), .f(seven_2_f), .g(seven_2_g));
  and and_11 (and_11_out, not_5_out, not_6_out, not_7_out, not_8_out);
  _7_Segment_Display u_7_segment_display_3 (
    .g(seven_3_g), .f(seven_3_f), .a(seven_3_a), .b(seven_3_b), .e(seven_3_e), .d(seven_3_d), .c(seven_3_c));  // open: dp
  _7_Segment_Display u_7_segment_display_4 (
    .g(seven_2_g), .f(seven_2_f), .a(seven_2_a), .b(seven_2_b), .e(seven_2_e), .d(seven_2_d), .c(seven_2_c));  // open: dp
  seven seven_3 (
    .W(j_k_ff_10_q), .X(j_k_ff_8_q), .Y(j_k_ff_4_q), .Z(j_k_ff_3_q), .a(seven_3_a), .b(seven_3_b),
    .c(seven_3_c), .d(seven_3_d), .e(seven_3_e), .f(seven_3_f), .g(seven_3_g));
  _7_Segment_Display u_7_segment_display_5 (
    .g(seven_1_g), .f(seven_1_f), .a(seven_1_a), .b(seven_1_b), .e(seven_1_e), .d(seven_1_d), .c(seven_1_c),
    .dp(seven_1_c));
  _7_Segment_Display u_7_segment_display_6 (
    .g(seven_3_g), .f(seven_3_f), .a(seven_3_a), .b(seven_3_b), .e(seven_3_e), .d(seven_3_d), .c(seven_3_c));  // open: dp

  // Notes on the sheet:
  //   FARE
  //   .
  //   DISTANCE
endmodule

module seven (
  input  W,
  input  X,
  input  Y,
  input  Z,
  output a,
  output b,
  output c,
  output d,
  output e,
  output f,
  output g
);

  wire and_1_out, and_2_out, and_3_out, and_4_out, and_5_out, and_6_out, and_7_out, and_8_out, and_9_out,
       and_10_out, and_11_out, and_12_out, and_13_out, and_14_out, and_15_out, and_16_out, and_17_out,
       not_1_out, not_2_out, not_3_out, not_4_out, not_5_out, not_6_out, not_7_out, not_8_out, not_9_out,
       not_10_out, not_11_out, not_12_out, not_13_out, not_14_out, not_15_out, not_16_out, not_17_out,
       not_18_out, not_19_out, not_20_out, not_21_out, not_22_out;

  not not_1 (not_1_out, X);
  and and_1 (and_1_out, not_1_out, not_2_out);
  not not_2 (not_2_out, Z);
  not not_3 (not_3_out, X);
  and and_2 (and_2_out, not_3_out, Y);
  and and_3 (and_3_out, X, Z);
  not not_4 (not_4_out, X);
  not not_5 (not_5_out, Y);
  and and_4 (and_4_out, not_5_out, not_6_out);
  not not_6 (not_6_out, Z);
  and and_5 (and_5_out, Y, Z);
  not not_7 (not_7_out, Y);
  or or_1 (c, not_7_out, Z, X);
  not not_8 (not_8_out, X);
  and and_6 (and_6_out, not_8_out, not_9_out);
  not not_9 (not_9_out, Z);
  not not_10 (not_10_out, X);
  and and_7 (and_7_out, not_10_out, Y);
  and and_8 (and_8_out, Y, not_11_out);
  not not_11 (not_11_out, Z);
  and and_9 (and_9_out, X, not_12_out, Z);
  not not_12 (not_12_out, Y);
  not not_13 (not_13_out, X);
  and and_10 (and_10_out, not_13_out, not_14_out);
  not not_14 (not_14_out, Z);
  and and_11 (and_11_out, Y, not_15_out);
  not not_15 (not_15_out, Z);
  not not_16 (not_16_out, Y);
  and and_12 (and_12_out, not_16_out, not_17_out);
  not not_17 (not_17_out, Z);
  and and_13 (and_13_out, X, not_18_out);
  not not_18 (not_18_out, Y);
  and and_14 (and_14_out, X, not_19_out);
  not not_19 (not_19_out, Z);
  not not_20 (not_20_out, X);
  and and_15 (and_15_out, not_20_out, Y);
  and and_16 (and_16_out, X, not_21_out);
  not not_21 (not_21_out, Y);
  and and_17 (and_17_out, X, not_22_out);
  not not_22 (not_22_out, Z);
  or or_2 (a, and_1_out, and_2_out, and_3_out, W);
  or or_3 (b, not_4_out, and_4_out, and_5_out);
  or or_4 (d, and_6_out, and_7_out, and_8_out, and_9_out);
  or or_5 (e, and_10_out, and_11_out);
  or or_6 (f, and_12_out, and_13_out, and_14_out, W);
  or or_7 (g, and_15_out, and_16_out, and_17_out, W);
endmodule

module counters (
);

  main main_1 ();
  main main_2 ();
endmodule
